// Logisim project PPI_Zadanie1_Vdovjak.circ as structural Verilog: 1 circuit, main circuit main
module main (
  input  A,
  input  B,
  input  C,
  input  D,
  output Y_zad,
  output Z_zad,
  output Y_DNF,
  output Z_DNF,
  output Y_KNF,
  output Z_KNF
);

  wire A_B_C_D_out, A_B_nC_nD_out, A_nC_nD_out, A_OR_B_out, ACD_out, B_nC_nD_out, B_nC_out, B_nD_out,
       B_XOR_D_out, BCD_out, C_XNOR_nD_out, nA_C_nD_out, nA_nB_nCD_out, nA_nBC_nD_out, nA_nC_D_out, nA_out,
       nB_C_nD_out, nB_C_out, nB_D_out, nB_nC_D_out, nB_nC_nD_out, nB_out, nC_out, nD_out;

  not nA (nA_out, A);
  not nC (nC_out, C);
  not nB (nB_out, B);
  not nD (nD_out, D);
  or A_B_nC_nD (A_B_nC_nD_out, A, B, nC_out, nD_out);
  or nA_C_nD (nA_C_nD_out, nA_out, C, nD_out);
  or nA_nC_D (nA_nC_D_out, nA_out, nC_out, D);
  or nB_C_nD (nB_C_nD_out, nB_out, C, nD_out);
  or A_OR_B (A_OR_B_out, A, B);
  xnor C_XNOR_nD (C_XNOR_nD_out, C, nD_out);
  xor B_XOR_D (B_XOR_D_out, B, D);
  and ACD (ACD_out, A, C, D);
  and BCD (BCD_out, B, C, D);
  and B_nC_nD (B_nC_nD_out, B, nC_out, nD_out);
  or A_B_C_D (A_B_C_D_out, A, B, C, D);
  or nB_nC_D (nB_nC_D_out, nB_out, nC_out, D);
  or B_nC (B_nC_out, B, nC_out);
  or nB_D (nB_D_out, nB_out, D);
  or B_nD (B_nD_out, B, nD_out);
  or nB_C (nB_C_out, nB_out, C);
  xor A_OR_B__XOR__C_XNOR_nD (Y_zad, A_OR_B_out, C_XNOR_nD_out);
  and nA_nBC_nD (nA_nBC_nD_out, nA_out, nB_out, C, nD_out);
  and nA_nB_nCD (nA_nB_nCD_out, nA_out, nB_out, nC_out, D);
  and A_nC_nD (A_nC_nD_out, A, nC_out, nD_out, nD_out);
  and nB_nC_nD (nB_nC_nD_out, nB_out, nC_out, nD_out);
  and A_B_C_D__A_B_nC_nD__nA_C_nD__nA_nC_D__nB_C_nD__nB_nC_D (Y_KNF, A_B_C_D_out, A_B_nC_nD_out, nA_C_nD_out, nA_nC_D_out, nB_C_nD_out, nB_nC_D_out);
  and B_nC__nB_D__B_nD__nB_C (Z_KNF, B_nC_out, nB_D_out, B_nD_out, nB_C_out);
  nor B_XOR_D__NOR__C_XNOR_nD (Z_zad, C_XNOR_nD_out, B_XOR_D_out);
  or nA_nBC_nD_nA_nB_nCD_ACD_BCD_A_nC_nD_nB_nC_nD (Y_DNF, nA_nBC_nD_out, nA_nB_nCD_out, ACD_out, BCD_out, A_nC_nD_out, B_nC_nD_out);
  or BCD___nB_nC_nD (Z_DNF, BCD_out, nB_nC_nD_out);

  // Notes on the sheet:
  //   DNF
  //   KNF
endmodule
