// Logisim project PPI_Zadanie2_Vdovjak.circ as structural Verilog: 1 circuit, main circuit main
module main (
  input  a,
  input  b,
  input  c,
  input  d,
  output A_2,
  output B_2,
  output C_2,
  output D_2,
  output E,
  output A_3,
  output B_3,
  output C_3,
  output D_3,
  output E_2
);

  wire a_b_out, b____c___d_out, na_2_out, na_out, nb_2_out, nb_out, nc_2_out, nc_out, nd_2_out, nd_out,
       \𝑎____𝑏_2_out , \𝑎____𝑏_out , \𝑎____𝑐___𝑑_out , \𝑎___𝑐_2_out , \𝑎___𝑐_out , \𝑎___𝑑_2_out ,
       \𝑎___𝑑_out , \𝑎__𝑐____𝑑_out , \𝑎__𝑐_out , \𝑎__𝑑_out , \𝑎_𝑐_out , \𝑏___𝑐__𝑑_out , \𝑏___𝑐_𝑑_out ,
       \𝑏___𝑑_out , \𝑏__𝑐____𝑑_out , \𝑏__𝑐_out , \𝑏__𝑑_out , \𝑏_𝑐_out , \𝑐__𝑑_out ;

  nand na (na_out, a, a);
  nor na_2 (na_2_out, a, a);
  nand nb (nb_out, b, b);
  nor nb_2 (nb_2_out, b, b);
  nand nc (nc_out, c, c);
  nor nc_2 (nc_2_out, c, c);
  nand nd (nd_out, d, d);
  nor nd_2 (nd_2_out, d, d);
  nand b____c___d (b____c___d_out, nb_out, nc_out, d);
  nand \u_𝑏___𝑐__𝑑  (\𝑏___𝑐__𝑑_out , nb_out, c, nd_out);
  nand a_b (a_b_out, a, b);
  nand \u_𝑎__𝑐____𝑑  (\𝑎__𝑐____𝑑_out , a, nc_out, nd_out);
  nand \u_𝑏__𝑐  (\𝑏__𝑐_out , b, nc_out);
  nand \u_𝑏___𝑐_𝑑  (\𝑏___𝑐_𝑑_out , nb_out, c, d);
  nand \u_𝑎___𝑐  (\𝑎___𝑐_out , na_out, c);
  nand \u_𝑎____𝑏  (\𝑎____𝑏_out , na_out, nb_out);
  nand \u_𝑏__𝑑  (\𝑏__𝑑_out , b, nd_out);
  nand \u_𝑎___𝑑  (\𝑎___𝑑_out , na_out, d, d);
  nor \u_𝑏__𝑐____𝑑  (\𝑏__𝑐____𝑑_out , b, nc_2_out, nd_2_out);
  nor \u_𝑎__𝑐  (\𝑎__𝑐_out , a, nc_2_out);
  nor \u_𝑎____𝑐___𝑑  (\𝑎____𝑐___𝑑_out , na_2_out, nc_2_out, d);
  nor \u_𝑏_𝑐  (\𝑏_𝑐_out , b, c);
  nor \u_𝑎_𝑐  (\𝑎_𝑐_out , a, c);
  nor \u_𝑐__𝑑  (\𝑐__𝑑_out , c, nd_2_out);
  nor \u_𝑎____𝑏_2  (\𝑎____𝑏_2_out , na_2_out, nb_2_out);
  nor \u_𝑎__𝑑  (\𝑎__𝑑_out , a, nd_2_out);
  nor \u_𝑎___𝑑_2  (\𝑎___𝑑_2_out , na_2_out, d);
  nor \u_𝑏___𝑑  (\𝑏___𝑑_out , nb_2_out, d);
  nor \u_𝑎___𝑐_2  (\𝑎___𝑐_2_out , na_2_out, c);
  nand \u_𝑎_𝑏____𝑏____𝑐___𝑑____𝑏___𝑐__𝑑_____𝑎__𝑐____𝑑  (A_2, b____c___d_out, \𝑏___𝑐__𝑑_out , a_b_out, \𝑎__𝑐____𝑑_out );
  nand \u_𝑎_𝑏___𝑏__𝑐______𝑏___𝑐_𝑑  (B_2, a_b_out, \𝑏__𝑐_out , \𝑏___𝑐_𝑑_out );
  nand \u_𝑎___𝑐____𝑏___𝑐_𝑑___𝑎__𝑐____𝑑  (C_2, \𝑎___𝑐_out , \𝑏___𝑐_𝑑_out , \𝑎__𝑐____𝑑_out );
  nand \u_𝑎____𝑏______𝑏____𝑐___𝑑___𝑏__𝑑  (D_2, \𝑎____𝑏_out , b____c___d_out, \𝑏__𝑑_out );
  nand \u_𝑎____𝑏______𝑎___𝑑____𝑏___𝑐__𝑑  (E, \𝑎____𝑏_out , \𝑎___𝑑_out , \𝑏___𝑐__𝑑_out );
  nor \u_𝑎__𝑏__𝑐____𝑑  (A_3, na_2_out, \𝑏__𝑐____𝑑_out );
  nor \u_𝑎__𝑐______𝑎____𝑐___𝑑___𝑏_𝑐  (B_3, \𝑎__𝑐_out , \𝑎____𝑐___𝑑_out , \𝑏_𝑐_out );
  nor \u_𝑎_𝑐___𝑐__𝑑______𝑎____𝑏______𝑎____𝑐___𝑑  (C_3, \𝑎____𝑐___𝑑_out , \𝑎_𝑐_out , \𝑐__𝑑_out , \𝑎____𝑏_2_out );
  nor \u_𝑎__𝑑______𝑎___𝑑____𝑎____𝑏_____𝑏__𝑐____𝑑  (D_3, \𝑎__𝑑_out , \𝑎___𝑑_2_out , \𝑎____𝑏_2_out , \𝑏__𝑐____𝑑_out );
  nor \u_𝑏___𝑑____𝑎____𝑏______𝑎___𝑐___𝑏__𝑐____𝑑  (E_2, \𝑏___𝑑_out , \𝑎____𝑏_2_out , \𝑎___𝑐_2_out , \𝑏__𝑐____𝑑_out );
endmodule
