// Logisim project PPI_Zadanie3_Vdovjak.circ as structural Verilog: 1 circuit, main circuit main
module main (
  input  X,
  input  RESET,
  output Y
);

  wire CLK_out, J1_out, J3_out, K1_out, K2_out, K3_out, nX_out, Z1____X_out, Z1____Z2____X_out,
       Z1____Z3___X_out, Z1_q, Z1_qn, Z1_Z2__Z3_out, Z1_Z2_X_out, Z1_Z3_X_out, Z2____Z3___X_out, Z2___X_out,
       Z2__X_out, Z2_q, Z2_qn, Z3__X_out, Z3_q, Z3_qn, Z3_X_out;

  nand nX (nX_out, X, X);
  Clock CLK (.out(CLK_out));
  nand Z1_Z2__Z3 (Z1_Z2__Z3_out, Z1_q, Z2_q, Z3_qn);
  nand Z3_X (Z3_X_out, X, Z3_q);
  nand Z2____Z3___X (Z2____Z3___X_out, Z3_qn, X, Z2_qn);
  nand Z2__X (Z2__X_out, Z2_q, nX_out);
  nand Z3__X (Z3__X_out, Z3_q, nX_out);
  nand Z1____Z3___X (Z1____Z3___X_out, Z1_qn, Z3_qn, X);
  nand Z1_Z3_X (Z1_Z3_X_out, Z1_q, Z3_q, X);
  nand Z1_Z2_X (Z1_Z2_X_out, Z1_q, Z2_q, X);
  nand Z1____Z2____X (Z1____Z2____X_out, Z1_qn, Z2_qn, nX_out);
  nand Z1____X (Z1____X_out, Z1_qn, nX_out);
  nand Z2___X (Z2___X_out, Z2_qn, X);
  nand u_Y (Y, Z1_Z2__Z3_out, Z1_Z2__Z3_out);
  nand J1 (J1_out, Z3_X_out, Z3_X_out);
  nand K1 (K1_out, Z2____Z3___X_out, Z2__X_out, Z3__X_out);
  nand K2 (K2_out, Z1____Z3___X_out, Z1_Z3_X_out);
  nand J3 (J3_out, Z1_Z2_X_out, Z1____Z2____X_out);
  nand K3 (K3_out, Z1____X_out, Z2___X_out);
  J_K_Flip_Flop Z1 (.J(J1_out), .clk(CLK_out), .K(K1_out), .Q(Z1_q), .Qn(Z1_qn), .reset(RESET));  // open: preset, en
  J_K_Flip_Flop Z2 (.J(nX_out), .clk(CLK_out), .K(K2_out), .Q(Z2_q), .Qn(Z2_qn), .preset(RESET));  // open: en, reset
  J_K_Flip_Flop Z3 (.J(J3_out), .clk(CLK_out), .K(K3_out), .Q(Z3_q), .Qn(Z3_qn), .reset(RESET));  // open: preset, en
endmodule
